# Fritzing sketch 02_rgb_mixer (saved by Fritzing 0.9.2b)
breadboards: 1

parts:
  R7 = Resistor [tolerance=±5% resistance=270 package=THT]
  R8 = Resistor [tolerance=±5% resistance=270 package=THT]
  R9 = Resistor [tolerance=±5% resistance=270 package=THT]
  MonkMakesDuino3 = MonkMakesDuino
  LED3 = RGB LED (com. anode, rbg) [package="5 mm [THT]"]
  S3 = Pushbutton [package="[SMD]"]

nets:
  N1: R7.Pin_0, LED3.red_cathode
  N2: R7.Pin_1, MonkMakesDuino3.6
  N3: R8.Pin_0, LED3.common_anode
  N4: R8.Pin_1, MonkMakesDuino3.5
  N5: R9.Pin_0, LED3.green_cathode
  N6: R9.Pin_1, MonkMakesDuino3.3
  N7: MonkMakesDuino3.A0, S3.Pin_2
  N8: MonkMakesDuino3.GND, LED3.blue_cathode, S3.Pin_1

custom parts:
  Pushbutton: A generic pushbutton.
