# Fritzing sketch 03_larson (saved by Fritzing 0.9.2b)
breadboards: 1

parts:
  LED13 = LEDs [package=led10mm]
  LED14 = LEDs [package=led10mm]
  LED15 = LEDs [package=led10mm]
  LED16 = LEDs [package=led10mm]
  LED17 = LEDs [package=led10mm]
  LED18 = LEDs [package=led10mm]
  LED19 = LEDs [package=led10mm]
  LED20 = LEDs [package=led10mm]
  LED21 = LEDs [package=led10mm]
  LED22 = LEDs [package=led10mm]
  LED23 = LEDs [package=led10mm]
  LED24 = LEDs [package=led10mm]
  R13 = Resistor [tolerance=±5% resistance=270 package=THT]
  R14 = Resistor [tolerance=±5% resistance=270 package=THT]
  R15 = Resistor [tolerance=±5% resistance=270 package=THT]
  R16 = Resistor [tolerance=±5% resistance=270 package=THT]
  R17 = Resistor [tolerance=±5% resistance=270 package=THT]
  R18 = Resistor [tolerance=±5% resistance=270 package=THT]
  R19 = Resistor [tolerance=±5% resistance=270 package=THT]
  R20 = Resistor [tolerance=±5% resistance=270 package=THT]
  R21 = Resistor [tolerance=±5% resistance=270 package=THT]
  R22 = Resistor [tolerance=±5% resistance=270 package=THT]
  R23 = Resistor [tolerance=±5% resistance=270 package=THT]
  R24 = Resistor [tolerance=±5% resistance=270 package=THT]
  POT2 = Breadboard Trimpot
  MonkMakesDuino2 = MonkMakesDuino

nets:
  N1: LED13.A, R19.Pin_0
  N2: LED13.C, LED14.C, LED15.C, LED16.C, LED17.C, LED18.C, LED19.C, LED20.C, LED21.C, LED22.C, LED23.C, LED24.C, POT2.PIN1, MonkMakesDuino2.GND
  N3: LED14.A, R13.Pin_0
  N4: LED15.A, R23.Pin_0
  N5: LED16.A, R17.Pin_0
  N6: LED17.A, R16.Pin_0
  N7: LED18.A, R20.Pin_0
  N8: LED19.A, R24.Pin_0
  N9: LED20.A, R15.Pin_0
  N10: LED21.A, R22.Pin_0
  N11: LED22.A, R21.Pin_0
  N12: LED23.A, R18.Pin_0
  N13: LED24.A, R14.Pin_0
  N14: R13.Pin_1, MonkMakesDuino2.13
  N15: R14.Pin_1, MonkMakesDuino2.10
  N16: R15.Pin_1, MonkMakesDuino2.2
  N17: R16.Pin_1, MonkMakesDuino2.9
  N18: R17.Pin_1, MonkMakesDuino2.11
  N19: R18.Pin_1, MonkMakesDuino2.5
  N20: R19.Pin_1, MonkMakesDuino2.12
  N21: R20.Pin_1, MonkMakesDuino2.7
  N22: R21.Pin_1, MonkMakesDuino2.8
  N23: R22.Pin_1, MonkMakesDuino2.4
  N24: R23.Pin_1, MonkMakesDuino2.3
  N25: R24.Pin_1, MonkMakesDuino2.6
  N26: POT2.PIN2, MonkMakesDuino2.A0
  N27: POT2.PIN3, MonkMakesDuino2.5V

custom parts:
  LEDs: LEDs Standard schematic elements and footprints for 5mm, 3mm, 1206, and 0603 sized LEDs. 5mm - Spark Fun Electronics SKU : COM-00529 (and others)
