# Fritzing sketch 04_lcd_message_board (saved by Fritzing 0.9.2b)
breadboards: 1

parts:
  MonkMakesDuino2 = MonkMakesDuino
  U1 = LCD-16X2 [package=lcd-16x2_noholes]
  R1 = Resistor [tolerance=±5% resistance=1k package=THT]

nets:
  N1: MonkMakesDuino2.3, U1.RS
  N2: MonkMakesDuino2.4, U1.E
  N3: MonkMakesDuino2.5, U1.DB4
  N4: MonkMakesDuino2.6, U1.DB5
  N5: MonkMakesDuino2.7, U1.DB6
  N6: MonkMakesDuino2.8, U1.DB7
  GND: MonkMakesDuino2.GND, U1.VSS, U1.R_W, U1.K, R1.Pin_0
  5V: MonkMakesDuino2.5V, U1.VDD, U1.A
  N7: U1.VO, R1.Pin_1

custom parts:
  LCD-16X2: Standard text-only 16x2 parallel input LCD
