# Fritzing sketch 05_lcd_thermometer (saved by Fritzing 0.9.2b)
breadboards: 1

parts:
  MonkMakesDuino2 = MonkMakesDuino
  T2 = TMP36 Temperature Sensor [package="TO92 [THT]"]
  C2 = Electrolytic Capacitor [capacitance=100μF package="0807 [SMD, electrolytic]"]
  U1 = LCD-16X2 [package=lcd-16x2_noholes]
  R2 = Resistor [tolerance=±5% resistance=1k package=THT]

nets:
  N1: MonkMakesDuino2.A3, T2.Vout
  N2: MonkMakesDuino2.3, U1.RS
  N3: MonkMakesDuino2.4, U1.E
  N4: MonkMakesDuino2.5, U1.DB4
  N5: MonkMakesDuino2.6, U1.DB5
  N6: MonkMakesDuino2.7, U1.DB6
  N7: MonkMakesDuino2.8, U1.DB7
  GND: MonkMakesDuino2.GND, T2.GND, C2.-, U1.VSS, U1.R_W, U1.K, R2.Pin_0
  5V: MonkMakesDuino2.5V, T2.+Vs, C2.+, U1.VDD, U1.A
  N8: U1.VO, R2.Pin_1

notes:
  +

custom parts:
  LCD-16X2: Standard text-only 16x2 parallel input LCD
