# Fritzing sketch 06_timer (saved by Fritzing 0.9.2b)
breadboards: 1

parts:
  S5 = Pushbutton [package="[SMD]"]
  MonkMakesDuino2 = MonkMakesDuino
  S6 = Piezo Buzzer
  U2 = LCD-16X2 [package=lcd-16x2_noholes]
  R3 = Resistor [tolerance=±5% resistance=1k package=THT]

nets:
  N1: S5.Pin_1, MonkMakesDuino2.A0
  N2: S5.Pin_2, MonkMakesDuino2.A2
  N3: MonkMakesDuino2.3, U2.RS
  N4: MonkMakesDuino2.4, U2.E
  N5: MonkMakesDuino2.5, U2.DB4
  N6: MonkMakesDuino2.6, U2.DB5
  N7: MonkMakesDuino2.7, U2.DB6
  N8: MonkMakesDuino2.8, U2.DB7
  N9: MonkMakesDuino2.11, S6.pin1
  GND: MonkMakesDuino2.GND, S6.pin2, U2.VSS, U2.R_W, U2.K, R3.Pin_0
  5V: MonkMakesDuino2.5V, U2.VDD, U2.A
  N10: U2.VO, R3.Pin_1

custom parts:
  Pushbutton: A generic pushbutton.
  Piezo Buzzer: Piezo Buzzer (PCB Mount)
  LCD-16X2: Standard text-only 16x2 parallel input LCD
