# Fritzing sketch 07_dice (saved by Fritzing 0.9.2b)
breadboards: 1

parts:
  R19 = Resistor [tolerance=±5% resistance=270 package=THT]
  MonkMakesDuino2 = MonkMakesDuino
  LED25 = LEDs [package=led10mm]
  LED26 = LEDs [package=led10mm]
  LED27 = LEDs [package=led10mm]
  R20 = Resistor [tolerance=±5% resistance=270 package=THT]
  R21 = Resistor [tolerance=±5% resistance=270 package=THT]
  LED28 = LEDs [package=led10mm]
  R22 = Resistor [tolerance=±5% resistance=270 package=THT]
  LED29 = LEDs [package=led10mm]
  R23 = Resistor [tolerance=±5% resistance=270 package=THT]
  LED30 = LEDs [package=led10mm]
  LED31 = LEDs [package=led10mm]
  R24 = Resistor [tolerance=±5% resistance=270 package=THT]
  R25 = Resistor [tolerance=±5% resistance=270 package=THT]
  S4 = Pushbutton [package="[SMD]"]

nets:
  N1: R19.Pin_0, LED25.A
  N2: R19.Pin_1, MonkMakesDuino2.13
  N3: MonkMakesDuino2.A2, S4.Pin_1
  N4: MonkMakesDuino2.6, R25.Pin_1
  N5: MonkMakesDuino2.7, R24.Pin_1
  N6: MonkMakesDuino2.8, R23.Pin_1
  N7: MonkMakesDuino2.10, R21.Pin_1
  N8: MonkMakesDuino2.11, R22.Pin_1
  N9: MonkMakesDuino2.12, R20.Pin_1
  N10: MonkMakesDuino2.GND, LED25.C, LED26.C, LED27.C, LED28.C, LED29.C, LED30.C, LED31.C, S4.Pin_2
  N11: LED26.A, R20.Pin_0
  N12: LED27.A, R21.Pin_0, LED28.A, R22.Pin_0
  N13: LED29.A, R23.Pin_0
  N14: LED30.A, R24.Pin_0
  N15: LED31.A, R25.Pin_0

custom parts:
  LEDs: LEDs Standard schematic elements and footprints for 5mm, 3mm, 1206, and 0603 sized LEDs. 5mm - Spark Fun Electronics SKU : COM-00529 (and others)
  Pushbutton: A generic pushbutton.
